// Logisim project loadheadcarry.circ as structural Verilog: 1 circuit, main circuit main
module main (
  input  X0,
  input  Yo,
  input  Co,
  input  x1,
  input  y1,
  input  x2,
  input  y2,
  input  x3,
  input  y3,
  output out_10,
  output out_11,
  output out_12,
  output out_13,
  output out_14,
  output out_15,
  output out_16,
  output out_17
);

  wire G1_out, G2_out, G3_out, Go_out, P1_out, P1Go_out, P1PoCo_out, P2_out, P2G1_out, P2P1Go_out,
       P2P1PoCo_out, P3_out, P3G3_out, P3P2G1_out, P3P2P1Go_out, P3P2P1PoCo_out, Po_out, PoCo_out;

  and Go (Go_out, X0, Yo);
  and G1 (G1_out, y1, x1);
  xor Po (Po_out, X0, Yo);
  and G2 (G2_out, x2, y2);
  xor P3 (P3_out, x3, y3);
  and G3 (G3_out, x3, y3);
  xor P1 (P1_out, x1, y1);
  xor P2 (P2_out, x2, y2);
  and P1Go (P1Go_out, P1_out, Go_out);
  and P2G1 (P2G1_out, P2_out, G1_out);
  xor S0 (out_10, Po_out, Co);
  and PoCo (PoCo_out, Po_out, Co);
  and P1PoCo (P1PoCo_out, P1_out, Co, Co);
  and P2P1Go (P2P1Go_out, P2_out, Go_out, P1_out);
  and P2P1PoCo (P2P1PoCo_out, Co, Co, P1_out, P2_out);
  or C1 (out_11, PoCo_out, Go_out);
  xor S1 (out_12, P1_out, out_11);
  or C2 (out_13, P1PoCo_out, G1_out, P1Go_out);
  and P3P2P1Go (P3P2P1Go_out, P1_out, P2_out, G1_out, P3_out);
  and P3G3 (P3G3_out, P3_out, G3_out);
  and P3P2G1 (P3P2G1_out, G1_out, P2_out, P3_out);
  and P3P2P1PoCo (P3P2P1PoCo_out, Co, P1_out, Co, P2_out, P3_out);
  xor S2 (out_14, P2_out, out_13);
  or C3 (out_15, G2_out, P2G1_out, P2P1PoCo_out, P2P1Go_out);
  xor S3 (out_16, P3_out, out_15);
  or C4 (out_17, P3P2P1PoCo_out, G3_out, P3P2P1Go_out, P3G3_out, P3P2G1_out);

  // Notes on the sheet:
  //   XoYo
endmodule
